// Logisim project conversor_pra_bcd.circ as structural Verilog: 3 circuits, main circuit main
module main (
  input  [7:0] in_1,
  output [3:0] out_2,
  output [3:0] out_3
);

  wire BCD_2_e, BCD_e, not_1_out, not_2_out, or_1_out, separador_out_9, separador_out_10, separador_out_11,
       separador_out_12, separador_out_13, separador_out_14, separador_out_15, separador_out_16;
  wire [3:0] BCD_2_s0, BCD_s0;

  Separador separador (
    .in_1(in_1[0]), .in_2(in_1[1]), .in_3(in_1[2]), .in_4(in_1[3]), .in_5(in_1[4]), .in_6(in_1[5]),
    .in_7(in_1[6]), .in_8(in_1[7]), .out_9(separador_out_9), .out_10(separador_out_10),
    .out_11(separador_out_11), .out_12(separador_out_12), .out_13(separador_out_13),
    .out_14(separador_out_14), .out_15(separador_out_15), .out_16(separador_out_16));
  BCD BCD (
    .A0(separador_out_13), .S0(BCD_s0[0]), .A1(separador_out_14), .S1(BCD_s0[1]), .A2(separador_out_15),
    .S2(BCD_s0[2]), .A3(separador_out_16), .S3(BCD_s0[3]), .E(BCD_e));
  BCD BCD_2 (
    .A0(separador_out_9), .S0(BCD_2_s0[0]), .A1(separador_out_10), .S1(BCD_2_s0[1]), .A2(separador_out_11),
    .S2(BCD_2_s0[2]), .A3(separador_out_12), .S3(BCD_2_s0[3]), .E(BCD_2_e));
  assign out_2 = not_1_out ? BCD_2_s0 : 4'bz;  // Controlled_Buffer controlled_buffer_1
  not not_1 (not_1_out, or_1_out);
  or or_1 (or_1_out, BCD_2_e, BCD_e);
  not not_2 (not_2_out, or_1_out);
  assign out_3 = not_2_out ? BCD_s0 : 4'bz;  // Controlled_Buffer controlled_buffer_2
endmodule

module BCD (
  input  A0,
  input  A1,
  input  A2,
  input  A3,
  output S0,
  output S1,
  output S2,
  output S3,
  output E
);

  wire and_1_out, and_2_out;

  and and_1 (and_1_out, A2, A3);
  and and_2 (and_2_out, A1, A3);
  or or_1 (E, and_1_out, and_2_out);

  assign S0 = A0;
  assign S1 = A1;
  assign S2 = A2;
  assign S3 = A3;
endmodule

module Separador (
  input  in_1,
  input  in_2,
  input  in_3,
  input  in_4,
  input  in_5,
  input  in_6,
  input  in_7,
  input  in_8,
  output out_9,
  output out_10,
  output out_11,
  output out_12,
  output out_13,
  output out_14,
  output out_15,
  output out_16
);

  wire [7:0] undriven;
  wire [7:4] divider_1_out, divider_1_rem;

  Divider divider_1 (
    .a({in_8, in_7, in_6, in_5, in_4, in_3, in_2, in_1}), .b(8'ha),
    .out({divider_1_out, out_12, out_11, out_10, out_9}), .upper(undriven),
    .rem({divider_1_rem, out_16, out_15, out_14, out_13}));
endmodule
